// Logisim project 4bitANDGate.circ as structural Verilog: 4 circuits, main circuit main
module main (
  input  [3:0] in_1,
  input  [3:0] in_2,
  output [3:0] out_3
);

  and and_1 (out_3[3], in_1[3], in_2[3]);
  and and_2 (out_3[2], in_1[2], in_2[2]);
  and and_3 (out_3[1], in_1[1], in_2[1]);
  and and_4 (out_3[0], in_1[0], in_2[0]);

  // Other names for the same wires on the sheet: A0 = in_1[0]; A1 = in_1[1]; A2 = in_1[2]; A3 = in_1[3]; B0 = in_2[0];
  //   B1 = in_2[1]; B2 = in_2[2]; B3 = in_2[3]; O0 = out_3[0]; O1 = out_3[1]; O2 = out_3[2]; O3 = out_3[3]
endmodule

module FourBitAdderSubtractor (
  input  in_1,
  input  [3:0] in_2,
  input  [3:0] in_3,
  output CARRY,
  output [3:0] out_5
);

  wire adder1bit_2_cout, adder1bit_3_cout, adder1bit_4_cout, xor_1_out, xor_2_out, xor_3_out, xor_4_out;

  xor xor_1 (xor_1_out, in_3[3], in_1);
  Adder1bit adder1bit_1 (.a(xor_1_out), .cin(adder1bit_2_cout), .b(in_2[3]), .cout(CARRY), .sum(out_5[3]));
  xor xor_2 (xor_2_out, in_3[2], in_1);
  Adder1bit adder1bit_2 (.a(xor_2_out), .cin(adder1bit_3_cout), .b(in_2[2]), .cout(adder1bit_2_cout), .sum(out_5[2]));
  xor xor_3 (xor_3_out, in_3[1], in_1);
  Adder1bit adder1bit_3 (.a(xor_3_out), .cin(adder1bit_4_cout), .b(in_2[1]), .cout(adder1bit_3_cout), .sum(out_5[1]));
  xor xor_4 (xor_4_out, in_3[0], in_1);
  Adder1bit adder1bit_4 (.a(xor_4_out), .cin(in_1), .b(in_2[0]), .cout(adder1bit_4_cout), .sum(out_5[0]));

  // Other names for the same wires on the sheet: A0 = in_2[0]; A1 = in_2[1]; A2 = in_2[2]; A3 = in_2[3]; B0 = in_3[0];
  //   B1 = in_3[1]; B2 = in_3[2]; B3 = in_3[3]; O0 = out_5[0]; O1 = out_5[1]; O2 = out_5[2]; O3 = out_5[3]
endmodule

module Adder1bit (
  input  cin,
  input  a,
  input  b,
  output sum,
  output cout
);

  Adder #(.width(1)) adder_1 (.a(a), .b(b), .out(sum), .cin(cin), .cout(cout));
endmodule

module LeftShifter (
  input  [3:0] in_1,
  input  [1:0] in_2,
  output [3:0] out_3
);

  Multiplexer #(.select(2)) multiplexer_1 (
    .in0(in_1[3]), .in1(in_1[2]), .in2(in_1[1]), .in3(in_1[0]), .out(out_3[3]), .sel(in_2));
  Multiplexer #(.select(2)) multiplexer_2 (
    .in0(in_1[2]), .in1(in_1[1]), .in2(in_1[0]), .in3(1'b0), .out(out_3[2]), .sel(in_2));
  Multiplexer #(.select(2)) multiplexer_3 (
    .in0(in_1[1]), .in1(in_1[0]), .in2(1'b0), .in3(1'b0), .out(out_3[1]), .sel(in_2));
  Multiplexer #(.select(2)) multiplexer_4 (
    .in0(in_1[0]), .in1(1'b0), .in2(1'b0), .in3(1'b0), .out(out_3[0]), .sel(in_2));

  // Other names for the same wires on the sheet: A0 = in_1[0]; A1 = in_1[1]; A2 = in_1[2]; A3 = in_1[3];
  //   O0 = out_3[0]; O1 = out_3[1]; O2 = out_3[2]; O3 = out_3[3]
endmodule
