// Logisim project CPU.circ as structural Verilog
module AND_3 (
  input  [2:0] A,
  input  [2:0] B,
  output [2:0] out_3
);

  and and_1 (out_3[0], A[0], B[0]);
  and and_2 (out_3[1], A[1], B[1]);
  and and_3 (out_3[2], A[2], B[2]);
endmodule

module OR_3 (
  input  [2:0] A,
  input  [2:0] B,
  output [2:0] out_3
);

  or or_1 (out_3[0], A[0], B[0]);
  or or_2 (out_3[1], A[1], B[1]);
  or or_3 (out_3[2], A[2], B[2]);
endmodule

module NOT_3 (
  input  [3:0] A,
  output [3:0] out_2
);

  not not_1 (out_2[0], A[0]);
  not not_2 (out_2[1], A[1]);
  not not_3 (out_2[2], A[2]);
  not not_4 (out_2[3], A[3]);
endmodule

module XOR_3 (
  input  [2:0] A,
  input  [2:0] B,
  output [2:0] out_3
);

  xor xor_1 (out_3[0], A[0], B[0]);
  xor xor_2 (out_3[1], A[1], B[1]);
  xor xor_3 (out_3[2], A[2], B[2]);
endmodule

module SHL_3 (
  input  [2:0] A,
  input  [2:0] B,
  output [2:0] O
);

  Multiplexer #(.select(2)) multiplexer_1 (.in0(A[2]), .in1(A[1]), .in2(A[0]), .in3(1'b0), .out(O[2]), .sel(B[1:0]));
  Multiplexer #(.select(2)) multiplexer_2 (.in0(A[1]), .in1(A[0]), .in2(1'b0), .in3(1'b0), .out(O[1]), .sel(B[1:0]));
  Multiplexer #(.select(2)) multiplexer_3 (.in0(A[0]), .in1(1'b0), .in2(1'b0), .in3(1'b0), .out(O[0]), .sel(B[1:0]));
endmodule

module SHR_3 (
  input  [3:0] A,
  input  [1:0] B,
  output [3:0] O
);

  Multiplexer #(.select(2)) multiplexer_1 (.in0(A[3]), .in1(A[3]), .in2(A[3]), .in3(A[3]), .out(O[3]), .sel(B));
  Multiplexer #(.select(2)) multiplexer_2 (.in0(A[2]), .in1(A[3]), .in2(A[3]), .in3(A[3]), .out(O[2]), .sel(B));
  Multiplexer #(.select(2)) multiplexer_3 (.in0(A[1]), .in1(A[2]), .in2(A[3]), .in3(A[3]), .out(O[1]), .sel(B));
  Multiplexer #(.select(2)) multiplexer_4 (.in0(A[0]), .in1(A[1]), .in2(A[2]), .in3(A[3]), .out(O[0]), .sel(B));
  // also tied to GND on the sheet: A[3]
endmodule

module ROL_3 (
  input  [3:0] A,
  input  [1:0] B,
  output [3:0] O
);

  Multiplexer #(.select(2)) multiplexer_1 (.in0(A[3]), .in1(A[2]), .in2(A[1]), .in3(A[0]), .out(O[3]), .sel(B));
  Multiplexer #(.select(2)) multiplexer_2 (.in0(A[2]), .in1(A[1]), .in2(A[0]), .in3(A[3]), .out(O[2]), .sel(B));
  Multiplexer #(.select(2)) multiplexer_3 (.in0(A[1]), .in1(A[0]), .in2(A[3]), .in3(A[2]), .out(O[1]), .sel(B));
  Multiplexer #(.select(2)) multiplexer_4 (.in0(A[0]), .in1(A[3]), .in2(A[2]), .in3(A[1]), .out(O[0]), .sel(B));
endmodule

module ROR_3 (
  input  [3:0] A,
  input  [1:0] B,
  output [3:0] O
);

  Multiplexer #(.select(2)) multiplexer_1 (.in0(A[3]), .in1(A[3]), .in2(A[1]), .in3(A[2]), .out(O[3]), .sel(B));
  Multiplexer #(.select(2)) multiplexer_2 (.in0(A[2]), .in1(A[3]), .in2(A[3]), .in3(A[1]), .out(O[2]), .sel(B));
  Multiplexer #(.select(2)) multiplexer_3 (.in0(A[1]), .in1(A[2]), .in2(A[3]), .in3(A[3]), .out(O[1]), .sel(B));
  Multiplexer #(.select(2)) multiplexer_4 (.in0(A[3]), .in1(A[1]), .in2(A[2]), .in3(A[3]), .out(O[0]), .sel(B));

  assign A[0] = A[3];

  // Other names for the same wires on the sheet: A0 = A[3]
endmodule

module Adder_1_bit (
  input  A,
  input  B,
  input  Cin,
  output S,
  output Cout
);

  wire and_1_out, and_2_out, xor_1_out;

  xor xor_1 (xor_1_out, A, B);
  xor xor_2 (S, xor_1_out, Cin);
  and and_1 (and_1_out, Cin, xor_1_out);
  and and_2 (and_2_out, A, B);
  or or_1 (Cout, and_1_out, and_2_out);
endmodule

module RAM_1x1 (
  input  Read_Select_1,
  input  Write_Data,
  input  Write_Select,
  input  CLK,
  input  Read_Select_2,
  output Read_Data_1,
  output Read_Data_2
);

  wire d_ff_1_q, multiplexer_1_out;

  Multiplexer multiplexer_1 (.in0(d_ff_1_q), .in1(Write_Data), .out(multiplexer_1_out), .sel(Write_Select));
  D_Flip_Flop d_ff_1 (.D(multiplexer_1_out), .clk(CLK), .Q(d_ff_1_q));  // open: Qn, preset, reset
  and and_1 (Read_Data_1, Read_Select_1, d_ff_1_q);
  and and_2 (Read_Data_2, d_ff_1_q, Read_Select_2);
endmodule

module RAM_1x16 (
  input  [15:0] Write_Data,
  input  Write_Select,
  input  Read_Select_1,
  input  Read_Select_2,
  input  Clock,
  output [15:0] RD1,
  output [15:0] RD2
);

  // SRAM_1x1 D3: pin names not known; wires that end beside it: Write_Data[3], Write_Select, Read_Select_1, Read_Select_2, RD1[3], RD2[3], Write_Data[2], Write_Select, Read_Select_1, Read_Select_2
  // SRAM_1x1 D7: pin names not known; wires that end beside it: Clock, Write_Data[7], Write_Select, Read_Select_1, Read_Select_2, RD1[7], RD2[7], Clock, Write_Data[6], Write_Select, Read_Select_1, Read_Select_2
  // SRAM_1x1 D11: pin names not known; wires that end beside it: Clock, Write_Data[11], Write_Select, Read_Select_1, Read_Select_2, RD1[11], RD2[11], Clock, Write_Data[10], Write_Select, Read_Select_1, Read_Select_2
  // SRAM_1x1 D15: pin names not known; wires that end beside it: Clock, Write_Data[15], Write_Select, Read_Select_1, Read_Select_2, Clock, RD1[15], RD2[15], Clock, Write_Data[14], Write_Select, Read_Select_1, Read_Select_2, Clock
  // SRAM_1x1 D2: pin names not known; wires that end beside it: RD1[2], RD2[2], Write_Data[1], Write_Select, Read_Select_1, Read_Select_2
  // SRAM_1x1 D6: pin names not known; wires that end beside it: RD1[6], RD2[6], Clock, Write_Data[5], Write_Select, Read_Select_1, Read_Select_2
  // SRAM_1x1 D10: pin names not known; wires that end beside it: RD1[10], RD2[10], Clock, Write_Data[9], Write_Select, Read_Select_1, Read_Select_2
  // SRAM_1x1 D14: pin names not known; wires that end beside it: RD1[14], RD2[14], Clock, Write_Data[13], Write_Select, Read_Select_1, Read_Select_2, Clock
  // SRAM_1x1 D1: pin names not known; wires that end beside it: RD1[1], RD2[1]
  // SRAM_1x1 D5: pin names not known; wires that end beside it: RD1[5], RD2[5]
  // SRAM_1x1 D9: pin names not known; wires that end beside it: RD1[9], RD2[9]
  // SRAM_1x1 D13: pin names not known; wires that end beside it: RD1[13], RD2[13]
  // SRAM_1x1 D0: pin names not known; wires that end beside it: Write_Data[0], Write_Select, Read_Select_1, Read_Select_2, RD1[0], RD2[0]
  // SRAM_1x1 D4: pin names not known; wires that end beside it: Clock, Write_Data[4], Write_Select, Read_Select_1, Read_Select_2, RD1[4], RD2[4]
  // SRAM_1x1 D8: pin names not known; wires that end beside it: Clock, Write_Data[8], Write_Select, Read_Select_1, Read_Select_2, RD1[8], RD2[8]
  // SRAM_1x1 D12: pin names not known; wires that end beside it: Clock, Write_Data[12], Write_Select, Read_Select_1, Read_Select_2, Clock, RD1[12], RD2[12]

  // Other names for the same wires on the sheet: RD_1_0 = RD1[0]; RD_1_1 = RD1[1]; RD_1_2 = RD1[2]; RD_1_3 = RD1[3];
  //   RD_1_4 = RD1[4]; RD_1_5 = RD1[5]; RD_1_6 = RD1[6]; RD_1_7 = RD1[7]; RD_1_8 = RD1[8]; RD_1_9 = RD1[9];
  //   RD_1_10 = RD1[10]; RD_1_11 = RD1[11]; RD_1_12 = RD1[12]; RD_1_13 = RD1[13]; RD_1_14 = RD1[14];
  //   RD_1_15 = RD1[15]; RD_2_0 = RD2[0]; RD_2_1 = RD2[1]; RD_2_2 = RD2[2]; RD_2_3 = RD2[3]; RD_2_4 = RD2[4];
  //   RD_2_5 = RD2[5]; RD_2_6 = RD2[6]; RD_2_7 = RD2[7]; RD_2_8 = RD2[8]; RD_2_9 = RD2[9]; RD_2_10 = RD2[10];
  //   RD_2_11 = RD2[11]; RD_2_12 = RD2[12]; RD_2_13 = RD2[13]; RD_2_14 = RD2[14]; RD_2_15 = RD2[15];
  //   RS1 = Read_Select_1; RS2 = Read_Select_2; WD0 = Write_Data[0]; WD1 = Write_Data[1]; WD2 = Write_Data[2];
  //   WD3 = Write_Data[3]; WD4 = Write_Data[4]; WD5 = Write_Data[5]; WD6 = Write_Data[6]; WD7 = Write_Data[7];
  //   WD8 = Write_Data[8]; WD9 = Write_Data[9]; WD10 = Write_Data[10]; WD11 = Write_Data[11]; WD12 = Write_Data[12];
  //   WD13 = Write_Data[13]; WD14 = Write_Data[14]; WD15 = Write_Data[15]; WS = Write_Select
endmodule

module RAM_8x16 (
  input  [15:0] WD,
  input  WE,
  input  [2:0] WA,
  input  [2:0] RA1,
  input  [2:0] RA2,
  input  CLK,
  output [15:0] RD1,
  output [15:0] RD2
);

  wire RA_1_0, RA_1_1, RA_1_2, RA_1_3, RA_1_4, RA_1_5, RA_1_6, RA_1_7, RA_2_0, RA_2_1, RA_2_2, RA_2_3,
       RA_2_4, RA_2_5, RA_2_6, RA_2_7, WS0, WS1, WS2, WS3, WS4, WS5, WS6, WS7;
  wire [15:0] RAM0_rd1, RAM0_rd2, RAM1_rd1, RAM1_rd2, RAM2_rd1, RAM2_rd2, RAM3_rd1, RAM3_rd2, RAM4_rd1,
       RAM4_rd2, RAM5_rd1, RAM5_rd2, RAM6_rd1, RAM6_rd2, RAM7_rd1, RAM7_rd2;

  Decoder #(.select(3)) decoder_1 (
    .out0(WS0), .out1(WS1), .out2(WS2), .out3(WS3), .out4(WS4), .out5(WS5), .out6(WS6), .out7(WS7), .sel(WA),
    .en(WE));
  Decoder #(.select(3)) decoder_2 (
    .out0(RA_1_0), .out1(RA_1_1), .out2(RA_1_2), .out3(RA_1_3), .out4(RA_1_4), .out5(RA_1_5), .out6(RA_1_6),
    .out7(RA_1_7), .sel(RA1));  // open: en
  Decoder #(.select(3)) decoder_3 (
    .out0(RA_2_0), .out1(RA_2_1), .out2(RA_2_2), .out3(RA_2_3), .out4(RA_2_4), .out5(RA_2_5), .out6(RA_2_6),
    .out7(RA_2_7), .sel(RA2));  // open: en
  RAM_1x16 RAM0 (
    .Read_Select_1(RA_1_0), .Read_Select_2(RA_2_0), .Write_Select(WS0), .Write_Data(WD), .Clock(CLK),
    .RD2(RAM0_rd2), .RD1(RAM0_rd1));
  RAM_1x16 RAM1 (
    .Read_Select_1(RA_1_1), .Read_Select_2(RA_2_1), .Write_Select(WS1), .Write_Data(WD), .Clock(CLK),
    .RD2(RAM1_rd2), .RD1(RAM1_rd1));
  RAM_1x16 RAM2 (
    .Read_Select_1(RA_1_2), .Read_Select_2(RA_2_2), .Write_Select(WS2), .Write_Data(WD), .Clock(CLK),
    .RD2(RAM2_rd2), .RD1(RAM2_rd1));
  RAM_1x16 RAM3 (
    .Read_Select_1(RA_1_3), .Read_Select_2(RA_2_3), .Write_Select(WS3), .Write_Data(WD), .Clock(CLK),
    .RD2(RAM3_rd2), .RD1(RAM3_rd1));
  RAM_1x16 RAM4 (
    .Read_Select_1(RA_1_4), .Read_Select_2(RA_2_4), .Write_Select(WS4), .Write_Data(WD), .Clock(CLK),
    .RD2(RAM4_rd2), .RD1(RAM4_rd1));
  RAM_1x16 RAM5 (
    .Read_Select_1(RA_1_5), .Read_Select_2(RA_2_5), .Write_Select(WS5), .Write_Data(WD), .Clock(CLK),
    .RD2(RAM5_rd2), .RD1(RAM5_rd1));
  RAM_1x16 RAM6 (
    .Read_Select_1(RA_1_6), .Read_Select_2(RA_2_6), .Write_Select(WS6), .Write_Data(WD), .Clock(CLK),
    .RD2(RAM6_rd2), .RD1(RAM6_rd1));
  RAM_1x16 RAM7 (
    .Read_Select_1(RA_1_7), .Read_Select_2(RA_2_7), .Write_Select(WS7), .Write_Data(WD), .Clock(CLK),
    .RD2(RAM7_rd2), .RD1(RAM7_rd1));
  assign RD1 = RAM0_rd1 | RAM1_rd1 | RAM2_rd1 | RAM3_rd1 | RAM4_rd1 | RAM5_rd1 | RAM6_rd1 | RAM7_rd1;  // OR_Gate or_1, 16 bits wide
  assign RD2 = RAM0_rd2 | RAM1_rd2 | RAM2_rd2 | RAM3_rd2 | RAM4_rd2 | RAM5_rd2 | RAM6_rd2 | RAM7_rd2;  // OR_Gate or_2, 16 bits wide
endmodule

module RF_1_bit (
  input  Din,
  input  Sel,
  input  CLK,
  output Dout
);

  wire multiplexer_1_out;

  D_Flip_Flop d_ff_1 (.D(multiplexer_1_out), .clk(CLK), .Q(Dout));  // open: Qn, preset, reset
  Multiplexer multiplexer_1 (.in0(Dout), .in1(Din), .out(multiplexer_1_out), .sel(Sel));
endmodule

module RF_4_bit (
  input  [3:0] Din,
  input  Sel,
  input  CLK,
  output [3:0] Dout
);

  RF_1_bit rf_1_bit_1 (.Sel(Sel), .Din(Din[0]), .CLK(CLK), .Dout(Dout[0]));
  RF_1_bit rf_1_bit_2 (.Sel(Sel), .Din(Din[1]), .CLK(CLK), .Dout(Dout[1]));
  RF_1_bit rf_1_bit_3 (.Sel(Sel), .Din(Din[2]), .CLK(CLK), .Dout(Dout[2]));
  RF_1_bit rf_1_bit_4 (.Sel(Sel), .Din(Din[3]), .CLK(CLK), .Dout(Dout[3]));
endmodule

module RF_SET_4Bit_with_8 (
  input  Reg_En,
  input  [2:0] Wr,
  input  [3:0] Wrd,
  input  CLK,
  input  [2:0] Ra,
  input  [2:0] Rb,
  output [3:0] A,
  output [3:0] B
);

  wire decoder_1_out0, decoder_1_out1, decoder_1_out2, decoder_1_out3, decoder_1_out4, decoder_1_out5,
       decoder_1_out6, decoder_1_out7;
  wire [3:0] R0_dout, R1_dout, R2_dout, R3_dout, R4_dout, R5_dout, R6_dout, R7_dout;

  Decoder #(.select(3)) decoder_1 (
    .out0(decoder_1_out0), .out1(decoder_1_out1), .out2(decoder_1_out2), .out3(decoder_1_out3),
    .out4(decoder_1_out4), .out5(decoder_1_out5), .out6(decoder_1_out6), .out7(decoder_1_out7), .sel(Wr),
    .en(Reg_En));
  RF_4_bit R0 (.Sel(decoder_1_out0), .CLK(CLK), .Din(Wrd), .Dout(R0_dout));
  RF_4_bit R1 (.Sel(decoder_1_out1), .CLK(CLK), .Din(Wrd), .Dout(R1_dout));
  RF_4_bit R2 (.Sel(decoder_1_out2), .CLK(CLK), .Din(Wrd), .Dout(R2_dout));
  RF_4_bit R3 (.Sel(decoder_1_out3), .CLK(CLK), .Din(Wrd), .Dout(R3_dout));
  RF_4_bit R4 (.Sel(decoder_1_out4), .CLK(CLK), .Din(Wrd), .Dout(R4_dout));
  RF_4_bit R5 (.Sel(decoder_1_out5), .CLK(CLK), .Din(Wrd), .Dout(R5_dout));
  RF_4_bit R6 (.Sel(decoder_1_out6), .CLK(CLK), .Din(Wrd), .Dout(R6_dout));
  RF_4_bit R7 (.Sel(decoder_1_out7), .CLK(CLK), .Din(Wrd), .Dout(R7_dout));
  Multiplexer #(.select(3), .width(4)) multiplexer_1 (
    .in0(R0_dout), .in1(R1_dout), .in2(R2_dout), .in3(R3_dout), .in4(R4_dout), .in5(R5_dout), .in6(R6_dout),
    .in7(R7_dout), .out(A), .sel(Ra));
  Multiplexer #(.select(3), .width(4)) multiplexer_2 (
    .in0(R0_dout), .in1(R1_dout), .in2(R2_dout), .in3(R3_dout), .in4(R4_dout), .in5(R5_dout), .in6(R6_dout),
    .in7(R7_dout), .out(B), .sel(Rb));
endmodule

module Adder_4 (
  input  [3:0] A,
  input  Sel,
  input  [3:0] B,
  output Carry,
  output [3:0] S
);

  wire adder_1_2_p1, adder_1_3_p1, adder_1_4_p1;

  // Adder_1 adder_1_1: pin names not known; wires that end beside it: Carry, A[3], S[3]
  // XOR_Gate xor_1 has open pins: in0=B[3], in1=Sel, out=open
  // Adder_1 adder_1_2: pin names not known; wires that end beside it: adder_1_2_p1, adder_1_2_p1, A[2], S[2]
  // XOR_Gate xor_2 has open pins: in0=B[2], in1=Sel, out=open
  // Adder_1 adder_1_3: pin names not known; wires that end beside it: adder_1_3_p1, adder_1_3_p1, A[1], S[1]
  // XOR_Gate xor_3 has open pins: in0=B[1], in1=Sel, out=open
  // Adder_1 adder_1_4: pin names not known; wires that end beside it: adder_1_4_p1, adder_1_4_p1, A[0], S[0], Sel
  // XOR_Gate xor_4 has open pins: in0=B[0], in1=Sel, out=open
endmodule

module SHL_4_bit (
  input  [3:0] A,
  input  [3:0] B,
  output [3:0] O
);

  Multiplexer #(.select(2)) multiplexer_1 (.in0(A[3]), .in1(A[2]), .in2(A[1]), .in3(A[0]), .out(O[3]), .sel(B[1:0]));
  Multiplexer #(.select(2)) multiplexer_2 (.in0(A[2]), .in1(A[1]), .in2(A[0]), .in3(1'b0), .out(O[2]), .sel(B[1:0]));
  Multiplexer #(.select(2)) multiplexer_3 (.in0(A[1]), .in1(A[0]), .in2(1'b0), .in3(1'b0), .out(O[1]), .sel(B[1:0]));
  Multiplexer #(.select(2)) multiplexer_4 (.in0(A[0]), .in1(1'b0), .in2(1'b0), .in3(1'b0), .out(O[0]), .sel(B[1:0]));
endmodule

module ALU_4 (
  input  [3:0] A,
  input  [3:0] B,
  input  [1:0] OP,
  output ZF,
  output SF,
  output [3:0] R,
  output CF
);

  wire [3:0] ADD, ANDR, NOTR, ORR, ROTL, ROTR, SHL, SHR, XORR;

  // AND_4 and_4_1: pin names not known; wires that end beside it: A, B, ANDR
  // OR_4 or_4_1: pin names not known; wires that end beside it: A, B, ORR
  // XOR_4 xor_4_1: pin names not known; wires that end beside it: A, B, XORR
  // NOT_4 not_4_1: pin names not known; wires that end beside it: A, NOTR
  Adder_4 adder_4_1 (.Sel(OP[0]), .B(B), .A(A), .Carry(CF), .S(ADD));
  SHL_4_bit shl_4_bit_1 (.B(B), .A(A), .O(SHL));
  SHR_4_bit shr_4_bit_1 (.B(B), .A(A), .O(SHR));
  ROL_4_bit rol_4_bit_1 (.B(B), .A(A), .O(ROTL));
  ROR_4_bit ror_4_bit_1 (.A(A), .B(B), .O(ROTR));
  Multiplexer #(.select(2), .width(4)) multiplexer_1 (.in0(ADD), .in1(ADD), .in2(SHL), .out(R), .sel(OP));  // open: in3
  nand nand_1 (ZF, R[0], R[1], R[2], R[3]);

  assign SF = R[3];

  // Other names for the same wires on the sheet: Sel = OP[0]
endmodule

module SHR_4_bit (
  input  [3:0] A,
  input  [3:0] B,
  output [3:0] O
);

  Multiplexer #(.select(2)) multiplexer_1 (.in0(A[3]), .in1(A[3]), .in2(A[3]), .in3(A[3]), .out(O[3]), .sel(B[1:0]));
  Multiplexer #(.select(2)) multiplexer_2 (.in0(A[2]), .in1(A[3]), .in2(A[3]), .in3(A[3]), .out(O[2]), .sel(B[1:0]));
  Multiplexer #(.select(2)) multiplexer_3 (.in0(A[1]), .in1(A[2]), .in2(A[3]), .in3(A[3]), .out(O[1]), .sel(B[1:0]));
  Multiplexer #(.select(2)) multiplexer_4 (.in0(A[0]), .in1(A[1]), .in2(A[2]), .in3(A[3]), .out(O[0]), .sel(B[1:0]));
  // also tied to GND on the sheet: A[3]
endmodule

module ROL_4_bit (
  input  [3:0] A,
  input  [3:0] B,
  output [3:0] O
);

  Multiplexer #(.select(2)) multiplexer_1 (.in0(A[3]), .in1(A[2]), .in2(A[1]), .in3(A[0]), .out(O[3]), .sel(B[1:0]));
  Multiplexer #(.select(2)) multiplexer_2 (.in0(A[2]), .in1(A[1]), .in2(A[0]), .in3(A[3]), .out(O[2]), .sel(B[1:0]));
  Multiplexer #(.select(2)) multiplexer_3 (.in0(A[1]), .in1(A[0]), .in2(A[3]), .in3(A[2]), .out(O[1]), .sel(B[1:0]));
  Multiplexer #(.select(2)) multiplexer_4 (.in0(A[0]), .in1(A[3]), .in2(A[2]), .in3(A[1]), .out(O[0]), .sel(B[1:0]));
endmodule

module ROR_4_bit (
  input  [3:0] A,
  input  [3:0] B,
  output [3:0] O
);

  Multiplexer #(.select(2)) multiplexer_1 (.in0(A[3]), .in1(A[3]), .in2(A[1]), .in3(A[2]), .out(O[3]), .sel(B[1:0]));
  Multiplexer #(.select(2)) multiplexer_2 (.in0(A[2]), .in1(A[3]), .in2(A[3]), .in3(A[1]), .out(O[2]), .sel(B[1:0]));
  Multiplexer #(.select(2)) multiplexer_3 (.in0(A[1]), .in1(A[2]), .in2(A[3]), .in3(A[3]), .out(O[1]), .sel(B[1:0]));
  Multiplexer #(.select(2)) multiplexer_4 (.in0(A[3]), .in1(A[1]), .in2(A[2]), .in3(A[3]), .out(O[0]), .sel(B[1:0]));

  assign A[0] = A[3];

  // Other names for the same wires on the sheet: A0 = A[3]
endmodule

module FLAG_REG (
  input  CF,
  input  ZF,
  input  SF,
  input  CLK,
  output C,
  output Z,
  output S
);

  RF_1_bit rf_1_bit_1 (.Sel(1'b1), .Din(CF), .CLK(CLK), .Dout(C));
  RF_1_bit rf_1_bit_2 (.Sel(1'b1), .Din(ZF), .CLK(CLK), .Dout(Z));
  RF_1_bit rf_1_bit_3 (.Sel(1'b1), .Din(SF), .CLK(CLK), .Dout(S));
endmodule

module PC (
  input  CLK,
  input  [2:0] Din,
  output [2:0] Dout
);

  D_Flip_Flop d_ff_1 (.clk(CLK), .D(Din[0]), .Q(Dout[0]));  // open: Qn, preset, reset
  D_Flip_Flop d_ff_2 (.clk(CLK), .D(Din[1]), .Q(Dout[1]));  // open: Qn, preset, reset
  D_Flip_Flop d_ff_3 (.clk(CLK), .D(Din[2]), .Q(Dout[2]));  // open: Qn, preset, reset
endmodule

module CPU_4 (
);

  wire [2:0] adder_1_out, pc_1_dout;

  Adder #(.width(3)) adder_1 (.a(pc_1_dout), .b(3'b001), .out(adder_1_out));  // open: cin, cout
  PC pc_1 (.Din(adder_1_out), .Dout(pc_1_dout));  // open: CLK
  RAM_8x16 ram_8x16_1 (.RA1(pc_1_dout));  // open: RA2, WA, CLK, WE, WD, RD1, RD2
endmodule
