// Logisim project Reg4bit5set.circ as structural Verilog: 4 circuits, main circuit main
module main (
  input  Din,
  input  Sel,
  input  CLK,
  output Dout
);

  wire multiplexer_1_out;

  D_Flip_Flop d_ff_1 (.D(multiplexer_1_out), .clk(CLK), .Q(Dout));  // open: Qn, preset, reset
  Multiplexer multiplexer_1 (.in0(Dout), .in1(Din), .out(multiplexer_1_out), .sel(Sel));
endmodule

module RF_1_Bit (
  input  Din,
  input  Sel,
  input  CLK,
  output Dout
);

  wire multiplexer_1_out;

  D_Flip_Flop d_ff_1 (.D(multiplexer_1_out), .clk(CLK), .Q(Dout));  // open: Qn, preset, reset
  Multiplexer multiplexer_1 (.in0(Dout), .in1(Din), .out(multiplexer_1_out), .sel(Sel));
endmodule

module RF_4_Bit (
  input  [3:0] Din,
  input  Sel,
  input  CLK,
  output [3:0] Dout
);

  RF_1_Bit rf_1_bit_1 (.Sel(Sel), .Din(Din[0]), .CLK(CLK), .Dout(Dout[0]));
  RF_1_Bit rf_1_bit_2 (.Sel(Sel), .Din(Din[1]), .CLK(CLK), .Dout(Dout[1]));
  RF_1_Bit rf_1_bit_3 (.Sel(Sel), .Din(Din[2]), .CLK(CLK), .Dout(Dout[2]));
  RF_1_Bit rf_1_bit_4 (.Sel(Sel), .Din(Din[3]), .CLK(CLK), .Dout(Dout[3]));
endmodule

module RF_4_Bit_8 (
  input  Reg_En,
  input  [2:0] Wr,
  input  [3:0] Wrd,
  input  CLK,
  input  [2:0] Ra,
  input  [2:0] Rb,
  output [3:0] A,
  output [3:0] B
);

  wire R0, R1, R2, R3, R4;
  wire [3:0] D0, D1, D2, D3, D4;

  Decoder #(.select(3)) decoder_1 (
    .out0(R0), .out1(R1), .out2(R2), .out3(R3), .out4(R4), .sel(Wr), .en(Reg_En));  // open: out5, out6, out7
  RF_4_Bit rf_4_bit_1 (.Sel(R0), .CLK(CLK), .Din(Wrd), .Dout(D0));
  RF_4_Bit rf_4_bit_2 (.Sel(R1), .CLK(CLK), .Din(Wrd), .Dout(D1));
  RF_4_Bit rf_4_bit_3 (.Sel(R2), .CLK(CLK), .Din(Wrd), .Dout(D2));
  RF_4_Bit rf_4_bit_4 (.Sel(R3), .CLK(CLK), .Din(Wrd), .Dout(D3));
  RF_4_Bit rf_4_bit_5 (.Sel(R4), .CLK(CLK), .Din(Wrd), .Dout(D4));
  Multiplexer #(.select(3), .width(4)) multiplexer_1 (
    .in0(D0), .in1(D1), .in2(D2), .in3(D3), .in4(D4), .out(A), .sel(Ra));  // open: in5, in6, in7
  Multiplexer #(.select(3), .width(4)) multiplexer_2 (
    .in0(D0), .in1(D1), .in2(D2), .in3(D3), .in4(D4), .out(B), .sel(Rb));  // open: in5, in6, in7
endmodule
