// Logisim project Registerset.circ as structural Verilog
module Reg1bit (
  input  Din,
  input  Sel,
  input  Clock,
  output Dout
);

  wire multiplexer_1_out;

  D_Flip_Flop d_ff_1 (.D(multiplexer_1_out), .clk(Clock), .Q(Dout));  // open: Qn, preset, reset
  Multiplexer multiplexer_1 (.in0(Dout), .in1(Din), .out(multiplexer_1_out), .sel(Sel));
endmodule
